// Logisim project Alarme_Simples.circ as structural Verilog: 1 circuit, main circuit main
module main (
  input  A,
  input  B,
  input  C
);

  wire and_1_out, or_1_out;

  or or_1 (or_1_out, A, B);
  and and_1 (and_1_out, or_1_out, C);
  LED led_1 (.in(and_1_out));

  // Notes on the sheet:
  //   A = 0 Porta Fechada
  //   A = 1 Porta Aberta
  //   B = 0 Sem Movimento
  //   B = 1 Movimento Detectado
  //   C = 0 Chave Desligada
  //   C = 1 Chave Ligada
endmodule
